// Logisim project my_circ.circ as structural Verilog: 1 circuit, main circuit main
module main (
  input  A,
  input  B,
  input  C,
  input  D,
  output Y,
  output Z,
  output DNF_Y,
  output DNF_Z
);

  wire and_1_out, and_2_out, and_3_out, and_4_out, and_5_out, and_6_out, nand_1_out, nor_1_out, not_1_out,
       not_2_out, not_3_out, not_4_out, or_1_out;

  not not_1 (not_1_out, D);
  not not_2 (not_2_out, B);
  not not_3 (not_3_out, C);
  not not_4 (not_4_out, A);
  and and_1 (and_1_out, not_2_out, C);
  and and_2 (and_2_out, not_3_out, B);
  or or_1 (or_1_out, A, B);
  nand nand_1 (nand_1_out, C, not_1_out);
  nor nor_1 (nor_1_out, B, D);
  and and_3 (and_3_out, not_4_out, not_2_out, C, not_1_out);
  and and_4 (and_4_out, B, D);
  and and_5 (and_5_out, A, not_3_out);
  and and_6 (and_6_out, A, D);
  xnor xnor_1 (Y, or_1_out, nand_1_out);
  xor xor_1 (Z, nand_1_out, nor_1_out);
  or or_2 (DNF_Y, and_1_out, and_2_out, D);
  or or_3 (DNF_Z, and_2_out, and_3_out, and_4_out, and_5_out, and_6_out);

  // Notes on the sheet:
  //   C!B+!CB+D
  //   !A!BC!D+B!C+BD+A!C+AD
endmodule
