// Logisim project 3_zad.circ as structural Verilog: 1 circuit, main circuit main
module main (
  input  X,
  input  Res,
  output Y
);

  wire CLK_out, j_k_ff_1_q, j_k_ff_2_q, j_k_ff_3_q, j_k_ff_3_qn, nand_1_out, nand_2_out, nand_3_out,
       nand_4_out, nand_6_out, nand_7_out, nand_8_out;

  nand nand_1 (nand_1_out, X, X);
  Clock CLK (.out(CLK_out));
  nand nand_2 (nand_2_out, nand_1_out, j_k_ff_2_q, j_k_ff_3_q);
  nand nand_3 (nand_3_out, X, j_k_ff_1_q);
  nand nand_4 (nand_4_out, nand_1_out, j_k_ff_3_q);
  nand nand_5 (Y, nand_3_out, nand_3_out);
  nand nand_6 (nand_6_out, nand_2_out, nand_2_out);
  nand nand_7 (nand_7_out, nand_3_out, nand_4_out);
  nand nand_8 (nand_8_out, X, j_k_ff_3_qn);
  J_K_Flip_Flop j_k_ff_1 (
    .J(nand_6_out), .clk(CLK_out), .K(1'b1), .Q(j_k_ff_1_q), .reset(Res));  // open: Qn, preset, en
  J_K_Flip_Flop j_k_ff_2 (
    .J(nand_7_out), .clk(CLK_out), .K(nand_8_out), .Q(j_k_ff_2_q), .reset(Res));  // open: Qn, preset, en
  J_K_Flip_Flop j_k_ff_3 (
    .J(X), .clk(CLK_out), .K(nand_1_out), .Q(j_k_ff_3_q), .Qn(j_k_ff_3_qn), .reset(Res));  // open: preset, en
endmodule
